// Logisim project BC.circ as structural Verilog
module main (
);

  CLK clk_1 ();  // open: CLOCK_IN, HALT, CLOCK_OUT
endmodule

module CLK (
  input  CLOCK_IN,
  input  HALT,
  output CLOCK_OUT
);

  wire not_1_out;

  not not_1 (not_1_out, HALT);
  and and_1 (CLOCK_OUT, CLOCK_IN, not_1_out);
endmodule
